# Fritzing sketch lunchbeat0 (saved by Fritzing 0.8.3b)
perfboards: 7

parts:
  R1 = Resistor [tolerance=±5% resistance=100k package=THT]
  U1 = 74HC595 [package="DIP16 [THT]"]
  U2 = LM 358 Dual Op-Amp [package="DIP8 [THT]"]
  U3 = atmega328 [package=dip]
  R4 = Trimmer Potentiometer [package=THT]
  R5 = Trimmer Potentiometer [package=THT]
  R6 = Trimmer Potentiometer [package=THT]
  R8 = Trimmer Potentiometer [package=THT]
  R10 = Trimmer Potentiometer [package=THT]
  HIHAT = Pushbutton [package="[THT]"]
  SNARE = Pushbutton [package="[THT]"]
  KICK = Pushbutton [package="[THT]"]
  RESET = Pushbutton [package="[THT]"]
  BASS = Pushbutton [package="[THT]"]
  LED8 = LED - 5mm [color="Blue (525nm)" package="5 mm [THT]"]
  R9 = Resistor [tolerance=±5% resistance=10k package=THT]
  PLAY = Pushbutton [package="[THT]"]
  C3 = Ceramic Capacitor [capacitance=22pF package="100 mil [THT, multilayer]"]
  C4 = Ceramic Capacitor [capacitance=22pF package="100 mil [THT, multilayer]"]
  EDIT = Pushbutton [package="[THT]"]
  R11 = Resistor [tolerance=±5% resistance=100k package=THT]
  R12 = Resistor [tolerance=±5% resistance=100k package=THT]
  R13 = Resistor [tolerance=±5% resistance=100k package=THT]
  R14 = Resistor [tolerance=±5% resistance=100k package=THT]
  R15 = Resistor [tolerance=±5% resistance=100k package=THT]
  R16 = Resistor [tolerance=±5% resistance=100k package=THT]
  R17 = Resistor [tolerance=±5% resistance=100k package=THT]
  TRS1 = Audio Jack (TRS) 3.5mm [package="PG203J [THT]"]
  C5 = Electrolytic Capacitor [capacitance=10µF package="100 mil [THT, electrolytic]"]
  R18 = Resistor [tolerance=±5% resistance=220 package=THT]
  LED9 = LED - 5mm [color="Blue (525nm)" package="5 mm [THT]"]
  R19 = Resistor [tolerance=±5% resistance=220 package=THT]
  LED10 = LED - 5mm [color="Blue (525nm)" package="5 mm [THT]"]
  R20 = Resistor [tolerance=±5% resistance=220 package=THT]
  LED11 = LED - 5mm [color="Blue (525nm)" package="5 mm [THT]"]
  R21 = Resistor [tolerance=±5% resistance=220 package=THT]
  LED12 = LED - 5mm [color="Blue (525nm)" package="5 mm [THT]"]
  R22 = Resistor [tolerance=±5% resistance=220 package=THT]
  LED13 = LED - 5mm [color="Blue (525nm)" package="5 mm [THT]"]
  R23 = Resistor [tolerance=±5% resistance=220 package=THT]
  LED14 = LED - 5mm [color="Blue (525nm)" package="5 mm [THT]"]
  R24 = Resistor [tolerance=±5% resistance=220 package=THT]
  LED15 = LED - 5mm [color="Blue (525nm)" package="5 mm [THT]"]
  R25 = Resistor [tolerance=±5% resistance=220 package=THT]
  XTAL1 = Crystal [frequency="16 MHz" package=THT]
  U4 = Voltage Regulator - 5V [package="DPak [SMD]"]
  C6 = Ceramic Capacitor [capacitance=0.1µF package="100 mil [THT, multilayer]"]
  C7 = Ceramic Capacitor [capacitance=47µF package="100 mil [THT, multilayer]"]
  C8 = Electrolytic Capacitor [capacitance=1µF package="100 mil [THT, electrolytic]"]
  D1 = Rectifier Diode [part_number=1N4001 package="300 mil [THT]"]
  Power = Power plug [part_number=PJ-002A]

nets:
  N1: R1.Pin_0, U3.D5_(PWM)
  N2: R1.Pin_1, R14.Pin_1, R15.Pin_1, R16.Pin_0
  N3: U1.Q1, LED8.anode
  N4: U1.Q2, LED9.anode
  N5: U1.Q3, LED10.anode
  N6: U1.Q4, LED11.anode
  N7: U1.Q5, LED12.anode
  N8: U1.Q6, LED14.anode
  N9: U1.Q7, LED15.anode
  GND: U1.GND, U1.OE, U2.connector3, U3.GND, R4.leg1, R5.leg1, R6.leg1, R8.leg1, R10.leg1, HIHAT.Pin_1, HIHAT.Pin_2, SNARE.Pin_1, SNARE.Pin_2, KICK.Pin_1, KICK.Pin_2, RESET.Pin_1, RESET.Pin_2, BASS.Pin_1, BASS.Pin_2, PLAY.Pin_1, PLAY.Pin_2, C3.0, C4.0, EDIT.Pin_3, EDIT.Pin_4, R16.Pin_1, TRS1.Sleeve, R18.Pin_0, R19.Pin_0, R20.Pin_0, R21.Pin_0, R22.Pin_0, R23.Pin_0, R24.Pin_0, R25.Pin_0, U4.GND, C6.0, C7.0, C8.-, Power.GND
  5V: U1.MR, U1.VCC, U2.connector7, U3.VCC, U3.AVCC, U3.AREF, R4.leg2, R5.leg2, R6.leg2, R8.leg2, R10.leg2, R9.Pin_0, U4.output_voltage, C6.1
  N10: U1.SH_CP, U3.D13
  N11: U1.ST_CP, U3.D10_(PWM)
  N12: U1.DS, U3.D11_(PWM)
  N13: U1.Q0, LED13.anode
  N14: U2.connector0, U2.connector1, C5.+
  N15: U2.connector2, R12.Pin_0, R13.Pin_0, R17.Pin_1
  N16: U3.RESET, RESET.Pin_3, RESET.Pin_4, R9.Pin_1
  N17: U3.D0_(RX), KICK.Pin_3, KICK.Pin_4
  N18: U3.D1_(TX), SNARE.Pin_3, SNARE.Pin_4
  N19: U3.D2, HIHAT.Pin_3, HIHAT.Pin_4
  N20: U3.D3_(PWM), BASS.Pin_3, BASS.Pin_4
  N21: U3.D4, PLAY.Pin_3, PLAY.Pin_4
  N22: U3.XLAT1, C4.1, XTAL1.pin_0
  N23: U3.XLAT2, C3.1, XTAL1.pin_1
  N24: U3.D6_(PWM), R11.Pin_0
  N25: U3.D7, R17.Pin_0
  N26: U3.D8, EDIT.Pin_1, EDIT.Pin_2
  N27: U3.A0, R8.wiper
  N28: U3.A1, R10.wiper
  N29: U3.A2, R6.wiper
  N30: U3.A3, R5.wiper
  N31: U3.A4, R4.wiper
  N32: LED8.cathode, R18.Pin_1
  N33: R11.Pin_1, R12.Pin_1, R13.Pin_1, R14.Pin_0, R15.Pin_0
  N34: TRS1.Ring, TRS1.Tip, C5.-
  N35: LED9.cathode, R19.Pin_1
  N36: LED10.cathode, R20.Pin_1
  N37: LED11.cathode, R21.Pin_1
  N38: LED12.cathode, R22.Pin_1
  N39: LED13.cathode, R23.Pin_1
  N40: LED14.cathode, R24.Pin_1
  N41: LED15.cathode, R25.Pin_1
  N42: U4.input_voltage, C7.1, C8.+, D1.cathode
  N43: D1.anode, Power.VCC

notes:
  RESET
  KICK
  SNARE
  HIHAT
  BASS
  PLAY
  AUDIO OUT
  LEDS AND DRIVER
  BRAIN
  POTS
  EDIT
  POWER
  R2R DAC LADDER
